// Logisim project 1a.circ as structural Verilog: 1 circuit, main circuit main
module main (
  input  x,
  input  y,
  input  z,
  output s
);

  wire and_1_out, and_2_out;

  and and_1 (and_1_out, x, z);
  and and_2 (and_2_out, y, z);
  or or_1 (s, and_1_out, and_2_out);
endmodule
