// Logisim project 1d.circ as structural Verilog: 1 circuit, main circuit main
module main (
  input  x,
  input  y,
  input  z,
  output s
);

  wire and_1_out, and_2_out, not_1_out, not_2_out;

  not not_1 (not_1_out, y);
  not not_2 (not_2_out, x);
  and and_1 (and_1_out, not_1_out, z);
  and and_2 (and_2_out, not_2_out, y);
  or or_1 (s, and_1_out, and_2_out);
endmodule
