// Logisim project 1e.circ as structural Verilog: 1 circuit, main circuit main
module main (
  input  x,
  input  y,
  input  z,
  output s
);

  wire and_1_out, and_2_out, not_1_out, not_2_out;

  not not_1 (not_1_out, x);
  not not_2 (not_2_out, z);
  and and_1 (and_1_out, x, z);
  and and_2 (and_2_out, not_1_out, not_2_out);
  or or_1 (s, and_1_out, and_2_out);
endmodule
