// Logisim project 2c.circ as structural Verilog: 1 circuit, main circuit main
module main (
  input  x,
  input  y,
  input  z,
  output s
);

  wire not_1_out, not_2_out, not_3_out, or_1_out, or_2_out, or_3_out;

  not not_1 (not_1_out, z);
  not not_2 (not_2_out, y);
  not not_3 (not_3_out, x);
  or or_1 (or_1_out, y, not_1_out);
  or or_2 (or_2_out, x, not_2_out, z);
  or or_3 (or_3_out, not_3_out, y);
  and and_1 (s, or_1_out, or_2_out, or_3_out);
endmodule
