// Logisim project 2d.circ as structural Verilog: 1 circuit, main circuit main
module main (
  input  x,
  input  y,
  input  z,
  output s
);

  wire not_1_out, not_2_out, not_3_out, not_4_out, or_1_out, or_2_out, or_3_out;

  not not_1 (not_1_out, y);
  not not_2 (not_2_out, z);
  not not_3 (not_3_out, x);
  not not_4 (not_4_out, y);
  or or_1 (or_1_out, x, y, z);
  or or_2 (or_2_out, not_1_out, not_2_out);
  or or_3 (or_3_out, not_3_out, not_4_out);
  and and_1 (s, or_1_out, or_2_out, or_3_out);
endmodule
