// Logisim project 2e.circ as structural Verilog: 1 circuit, main circuit main
module main (
  input  x,
  input  y,
  input  z,
  output s
);

  wire not_1_out, not_2_out, not_3_out, not_4_out, not_5_out, not_6_out, or_1_out, or_2_out, or_3_out,
       or_4_out;

  not not_1 (not_1_out, z);
  not not_2 (not_2_out, y);
  not not_3 (not_3_out, x);
  not not_4 (not_4_out, x);
  not not_5 (not_5_out, y);
  not not_6 (not_6_out, z);
  or or_1 (or_1_out, x, y, not_1_out);
  or or_2 (or_2_out, x, not_2_out, z);
  or or_3 (or_3_out, not_3_out, y, z);
  or or_4 (or_4_out, not_4_out, not_5_out, not_6_out);
  and and_1 (s, or_1_out, or_2_out, or_3_out, or_4_out);
endmodule
