// Logisim project 3d.circ as structural Verilog: 1 circuit, main circuit main
module main (
  input  x,
  input  y,
  input  w,
  input  z,
  output s
);

  wire and_1_out, and_2_out, and_3_out, and_4_out, not_1_out, not_2_out, not_3_out, not_4_out, not_5_out;

  not not_1 (not_1_out, y);
  and and_1 (and_1_out, not_1_out, w, not_2_out);
  not not_2 (not_2_out, z);
  not not_3 (not_3_out, x);
  and and_2 (and_2_out, not_3_out, y, z);
  not not_4 (not_4_out, y);
  and and_3 (and_3_out, x, not_4_out, w);
  and and_4 (and_4_out, x, w, not_5_out);
  not not_5 (not_5_out, z);
  or or_1 (s, and_1_out, and_2_out, and_3_out, and_4_out);
endmodule
