// Logisim project 4d.circ as structural Verilog: 1 circuit, main circuit main
module main (
  input  x,
  input  y,
  input  w,
  input  z,
  output s
);

  wire and_1_out, and_2_out, and_3_out, and_4_out, and_5_out, not_1_out, not_2_out, not_3_out, not_4_out,
       not_5_out, not_6_out, not_7_out, not_8_out;

  not not_1 (not_1_out, x);
  not not_2 (not_2_out, y);
  and and_1 (and_1_out, not_1_out, not_2_out, not_3_out);
  not not_3 (not_3_out, z);
  not not_4 (not_4_out, w);
  and and_2 (and_2_out, y, not_4_out, not_5_out);
  not not_5 (not_5_out, z);
  not not_6 (not_6_out, x);
  and and_3 (and_3_out, not_6_out, y, z);
  and and_4 (and_4_out, x, not_7_out, z);
  not not_7 (not_7_out, y);
  and and_5 (and_5_out, x, w, not_8_out);
  not not_8 (not_8_out, z);
  or or_1 (s, and_1_out, and_2_out, and_3_out, and_4_out, and_5_out);
endmodule
