// Logisim project 6_resposta.circ as structural Verilog: 1 circuit, main circuit main
module main (
  input  x,
  input  y,
  input  w,
  input  z,
  output s
);

  wire and_1_out, and_2_out, and_3_out, not_1_out, not_2_out, not_3_out;

  and and_1 (and_1_out, x, not_1_out);
  not not_1 (not_1_out, y);
  and and_2 (and_2_out, x, not_2_out);
  not not_2 (not_2_out, w);
  and and_3 (and_3_out, x, not_3_out);
  not not_3 (not_3_out, z);
  or or_1 (s, and_1_out, and_2_out, and_3_out);
endmodule
