// Logisim project 2.circ as structural Verilog: 1 circuit, main circuit main
module main (
  input  in_1,
  input  in_2,
  input  in_3,
  output out_4
);

  wire nand_1_out, nor_1_out;

  nand nand_1 (nand_1_out, in_1, in_3);
  nor nor_1 (nor_1_out, in_1, in_3);
  Multiplexer #(.enable("false")) multiplexer_1 (.in0(nor_1_out), .in1(nand_1_out), .out(out_4), .sel(in_2));
endmodule
