// Logisim project 5.circ as structural Verilog: 1 circuit, main circuit main
module main (
  input  in_1,
  input  in_2,
  input  [2:0] in_3,
  output out_4
);

  wire and_1_out, nand_1_out, nor_1_out, not_1_out, or_1_out, xnor_1_out, xor_1_out;

  not not_1 (not_1_out, in_1);
  and and_1 (and_1_out, in_1, in_2);
  nand nand_1 (nand_1_out, in_1, in_2);
  xor xor_1 (xor_1_out, in_1, in_2);
  xnor xnor_1 (xnor_1_out, in_1, in_2);
  or or_1 (or_1_out, in_1, in_2);
  nor nor_1 (nor_1_out, in_1, in_2);
  Multiplexer #(.select(3), .enable("false")) multiplexer_1 (
    .in0(not_1_out), .in1(and_1_out), .in2(nand_1_out), .in3(xor_1_out), .in4(xnor_1_out), .in5(or_1_out),
    .in6(nor_1_out), .out(out_4), .sel(in_3));  // open: in7
endmodule
