// Logisim project guia_exercicio01.circ as structural Verilog: 3 circuits, main circuit main
module main (
  input  in_1,
  input  in_2,
  output out_3,
  output out_4
);

  and and_1 (out_3, in_2, in_1);
  xor xor_1 (out_4, in_2, in_1);
endmodule

module somador_completo (
  input  A,
  input  B,
  input  CARRYIN,
  output SAIDA,
  output RESULTADO
);

  wire main_1_out_3, main_1_out_4, main_2_out_3;

  main main_1 (.in_1(B), .in_2(A), .out_3(main_1_out_3), .out_4(main_1_out_4));
  main main_2 (.in_1(main_1_out_4), .in_2(CARRYIN), .out_3(main_2_out_3), .out_4(RESULTADO));
  or or_1 (SAIDA, main_1_out_3, main_2_out_3);
endmodule

module somador_4b (
  input  in_1,
  input  in_2,
  input  in_3,
  input  in_4,
  input  in_5,
  input  in_6,
  input  in_7,
  input  in_8,
  output CarryOut,
  output out_10,
  output out_11,
  output out_12,
  output out_13
);

  wire somador_completo_2_saida, somador_completo_3_saida, somador_completo_4_saida;

  somador_completo somador_completo_1 (
    .A(in_5), .B(in_1), .CARRYIN(somador_completo_2_saida), .SAIDA(CarryOut), .RESULTADO(out_10));
  somador_completo somador_completo_2 (
    .A(in_6), .B(in_2), .CARRYIN(somador_completo_3_saida), .SAIDA(somador_completo_2_saida),
    .RESULTADO(out_11));
  somador_completo somador_completo_3 (
    .A(in_7), .B(in_3), .CARRYIN(somador_completo_4_saida), .SAIDA(somador_completo_3_saida),
    .RESULTADO(out_12));
  somador_completo somador_completo_4 (
    .A(in_8), .B(in_4), .CARRYIN(1'b0), .SAIDA(somador_completo_4_saida), .RESULTADO(out_13));

  // Notes on the sheet:
  //   A
  //   saida b1
  //   saida b2
  //   saida b3
  //   B
  //   saida b4
endmodule
