// Logisim project guia_exercicio02.circ as structural Verilog: 2 circuits, main circuit main
module main (
  input  in_1,
  input  in_2,
  input  BorrowIn,
  output diff,
  output BorrowOut
);

  wire and_1_out, and_2_out, and_3_out, not_1_out, not_2_out, xor_1_out;

  not not_1 (not_1_out, in_1);
  not not_2 (not_2_out, in_1);
  xor xor_1 (xor_1_out, in_1, in_2);
  and and_1 (and_1_out, in_2, BorrowIn);
  and and_2 (and_2_out, not_1_out, BorrowIn);
  and and_3 (and_3_out, not_2_out, in_2);
  xor xor_2 (diff, xor_1_out, BorrowIn);
  or or_1 (BorrowOut, and_1_out, and_2_out, and_3_out);
endmodule

module sub_6b (
  input  in_1,
  input  in_2,
  input  in_3,
  input  in_4,
  input  in_5,
  input  in_6,
  input  in_7,
  input  in_8,
  input  in_9,
  input  in_10,
  input  in_11,
  input  in_12,
  output out_13,
  output out_14,
  output out_15,
  output out_16,
  output out_17,
  output out_18,
  output out_19
);

  wire main_1_borrowout, main_2_borrowout, main_3_borrowout, main_4_borrowout, main_5_borrowout;

  main main_1 (.in_1(in_6), .in_2(in_7), .BorrowIn(1'b0), .diff(out_14), .BorrowOut(main_1_borrowout));
  main main_2 (.in_1(in_5), .in_2(in_8), .BorrowIn(main_1_borrowout), .diff(out_15), .BorrowOut(main_2_borrowout));
  main main_3 (.in_1(in_4), .in_2(in_9), .BorrowIn(main_2_borrowout), .diff(out_16), .BorrowOut(main_3_borrowout));
  main main_4 (.in_1(in_3), .in_2(in_10), .BorrowIn(main_3_borrowout), .diff(out_17), .BorrowOut(main_4_borrowout));
  main main_5 (.in_1(in_2), .in_2(in_11), .BorrowIn(main_4_borrowout), .diff(out_18), .BorrowOut(main_5_borrowout));
  main main_6 (.in_1(in_1), .in_2(in_12), .BorrowIn(main_5_borrowout), .diff(out_19), .BorrowOut(out_13));
endmodule
