// Logisim project guia_exercicio04.circ as structural Verilog: 2 circuits, main circuit main
module main (
  input  in_1,
  input  in_2,
  output out_3
);

  xor xor_1 (out_3, in_1, in_2);
endmodule

module comp_desigualdade (
  input  in_1,
  input  in_2,
  input  in_3,
  input  in_4,
  input  in_5,
  input  in_6,
  input  in_7,
  input  in_8,
  input  in_9,
  input  in_10,
  output out_11
);

  wire main_1_out_3, main_2_out_3, main_3_out_3, main_4_out_3, main_5_out_3;

  main main_1 (.in_1(in_5), .in_2(in_6), .out_3(main_1_out_3));
  main main_2 (.in_1(in_4), .in_2(in_7), .out_3(main_2_out_3));
  or or_1 (out_11, main_1_out_3, main_2_out_3, main_3_out_3, main_4_out_3, main_5_out_3);
  main main_3 (.in_1(in_3), .in_2(in_8), .out_3(main_3_out_3));
  main main_4 (.in_1(in_2), .in_2(in_9), .out_3(main_4_out_3));
  main main_5 (.in_1(in_1), .in_2(in_10), .out_3(main_5_out_3));
endmodule
