// Logisim project guia_exercicio05.circ as structural Verilog: 2 circuits, main circuit main
module main (
  input  in_1,
  input  carryIn,
  output out_3,
  output saida
);

  wire not_1_out;

  not not_1 (not_1_out, in_1);
  and and_1 (out_3, carryIn, not_1_out);
  xor xor_1 (saida, carryIn, not_1_out);

  // Notes on the sheet:
  //   A
  //   B
endmodule

module _6b (
  input  in_1,
  input  in_2,
  input  in_3,
  input  in_4,
  input  in_5,
  input  in_6,
  output out_7,
  output out_8,
  output out_9,
  output out_10,
  output out_11,
  output out_12
);

  wire main_1_out_3, main_2_out_3, main_3_out_3, main_4_out_3, main_5_out_3;

  main main_1 (.in_1(in_1), .carryIn(1'b1), .out_3(main_1_out_3), .saida(out_7));
  main main_2 (.in_1(main_1_out_3), .carryIn(in_2), .out_3(main_2_out_3), .saida(out_8));
  main main_3 (.in_1(main_2_out_3), .carryIn(in_3), .out_3(main_3_out_3), .saida(out_9));
  main main_4 (.in_1(main_3_out_3), .carryIn(in_4), .out_3(main_4_out_3), .saida(out_10));
  main main_5 (.in_1(main_4_out_3), .carryIn(in_5), .out_3(main_5_out_3), .saida(out_12));
  main main_6 (.in_1(main_5_out_3), .carryIn(in_6), .saida(out_11));  // open: out_3
endmodule
